# Fritzing sketch ESP8266_AnalogRead_MultipleSensors (saved by Fritzing 0.9.2b)
breadboards: 1

parts:
  U1 = NodeMCU V1.0
  R2 = Slide Potentiometer [maximum_resistance=100kΩ]
  R1 = Resistor [tolerance=±5% resistance=10k package=THT]
  D1 = Rectifier Diode [part_number=1N4007 package="300 mil [THT]"]
  R4 = Photocell (LDR) [package=THT]
  D2 = Rectifier Diode [part_number=1N4007 package="300 mil [THT]"]

nets:
  N1: U1.GND, R1.Pin_0
  N2: U1.D7, R4.pin_1
  N3: U1.D8, R2.leg1
  N4: U1.A0, R1.Pin_1, D1.cathode, D2.cathode
  N5: R2.wiper, D2.anode
  N6: D1.anode, R4.pin_0

custom parts:
  NodeMCU V1.0: ESP8266 based NodeMCU
